# Fritzing sketch DiseñoElectronico (saved by Fritzing 0.9.3b)
breadboards: 1

parts:
  Componente1 = Arduino Uno (Rev3)
  hc-sr1 = hc-sr04  # not connected
  S1 = H-Bridge with L298N
  M1 = DC Motor
  M2 = DC Motor
  VCC1 = Battery block 9V
  VCC2 = 4 x AAA Battery Mount

nets:
  GND: Componente1.GND, S1.GND, VCC1.-, VCC2.-
  N1: Componente1.D4, S1.IN1
  N2: Componente1.D5_PWM, S1.IN2
  N3: Componente1.D6_PWM, S1.IN3
  N4: Componente1.D7, S1.IN4
  N5: Componente1.VIN, VCC1.+
  N6: S1.12V, VCC2.+
  N7: S1.M1-01, M1.pin_2
  N8: S1.M1-02, M1.pin_1
  N9: S1.M2-01, M2.pin_2
  N10: S1.M2-02, M2.pin_1

custom parts:
  H-Bridge with L298N: h-bridge
