# Fritzing sketch DiseñoElectronico_v2 (saved by Fritzing 0.9.3b)
breadboards: 1

parts:
  Componente1 = Arduino Uno (Rev3)
  hc-sr1 = hc-sr04
  S1 = H-Bridge with L298N
  M1 = DC Motor
  M2 = DC Motor
  VCC1 = Battery block 9V
  VCC2 = 4 x AAA Battery Mount
  J1 = Basic Servo

nets:
  N1: Componente1.D11_PWM/MOSI, J1.pulse
  N2: Componente1.D12/MISO, hc-sr1.Trig
  N3: Componente1.D13/SCK, hc-sr1.Echo
  GND: Componente1.GND, hc-sr1.GND, S1.GND, VCC1.-, VCC2.-, J1.gnd
  N4: Componente1.D4, S1.IN1
  N5: Componente1.D5_PWM, S1.IN2
  N6: Componente1.D6_PWM, S1.IN3
  N7: Componente1.D7, S1.IN4
  VCC: Componente1.5V, hc-sr1.VCC, J1.vcc
  N8: Componente1.VIN, VCC1.+
  N9: S1.12V, VCC2.+
  N10: S1.M1-01, M1.pin_2
  N11: S1.M1-02, M1.pin_1
  N12: S1.M2-01, M2.pin_2
  N13: S1.M2-02, M2.pin_1

custom parts:
  H-Bridge with L298N: h-bridge
